// Logisim project LC-2200-16.circ as structural Verilog: 7 circuits, main circuit main
module main (
);

  wire CLK, comparator_1_eq, DrALU, DrMEM, DrOFF, DrPC, DrREG, LdA, LdB, LdIR, LdMAR, LdPC, LdZ, not_1_out,
       WrMEM, WrREG, Z;
  wire [1:0] func;
  wire [3:0] regno;
  wire [4:0] Dr_spl_in, microcontroller_1_outsignal;
  wire [5:0] Ld_spl_in;
  wire [15:0] A_q, alux16_1_output, B_q, bit_extender_1_out, controlled_buffer_1_out, IR_q, MAR_q, PC_q,
       ram_1_data, register_array_1_dout;

  Clock clock_1 (.out(CLK));
  Register #(.width(16)) PC (.D(controlled_buffer_1_out), .en(LdPC), .Q(PC_q), .clk(CLK));  // open: clr
  assign controlled_buffer_1_out = DrPC ? PC_q : 16'bz;  // Controlled_Buffer controlled_buffer_1
  Comparator #(.width(16)) comparator_1 (
    .a(controlled_buffer_1_out), .b({16{1'b0}}), .eq(comparator_1_eq));  // open: gt, lt
  Register #(.width(16)) A (.D(controlled_buffer_1_out), .en(LdA), .Q(A_q), .clk(CLK));  // open: clr
  ALUx16 alux16_1 (.func(func), .A(A_q), .B(B_q), .\output (alux16_1_output));
  assign controlled_buffer_1_out = DrALU ? alux16_1_output : 16'bz;  // Controlled_Buffer controlled_buffer_2
  D_Flip_Flop #(.trigger("high")) u_Z (.clk(CLK), .D(comparator_1_eq), .Q(Z), .en(LdZ));  // open: Qn, preset, reset
  Register #(.width(16)) B (.D(controlled_buffer_1_out), .en(LdB), .Q(B_q), .clk(CLK));  // open: clr
  Ld_split ld_split_1 (.Input(Ld_spl_in), .LdPC(LdPC), .LdIR(LdIR), .LdMAR(LdMAR), .LdA(LdA), .LdB(LdB), .LdZ(LdZ));
  Dr_split dr_split_1 (.Input(Dr_spl_in), .DrREG(DrREG), .DrOFF(DrOFF), .DrALU(DrALU), .DrMEM(DrMEM), .DrPC(DrPC));
  register_array register_array_1 (
    .WrREG(WrREG), .regno(regno), .Din(controlled_buffer_1_out), .Dout(register_array_1_dout), .CLK(CLK));
  assign controlled_buffer_1_out = DrREG ? register_array_1_dout : 16'bz;  // Controlled_Buffer controlled_buffer_3
  Register #(.width(16)) MAR (.D(controlled_buffer_1_out), .en(LdMAR), .Q(MAR_q), .clk(CLK));  // open: clr
  not not_1 (not_1_out, WrMEM);
  assign controlled_buffer_1_out = DrMEM ? ram_1_data : 16'bz;  // Controlled_Buffer controlled_buffer_4
  RAM #(.addrWidth(16), .dataWidth(16), .bus("separate")) ram_1 (
    .addr(MAR_q), .din(controlled_buffer_1_out), .data(ram_1_data), .str(WrMEM), .clk(CLK), .ld(not_1_out));  // open: sel, clr
  assign controlled_buffer_1_out = DrOFF ? bit_extender_1_out : 16'bz;  // Controlled_Buffer controlled_buffer_5
  Register #(.width(16)) IR (.D(controlled_buffer_1_out), .en(LdIR), .Q(IR_q), .clk(CLK));  // open: clr
  microcontroller microcontroller_1 (
    .Input_x16(IR_q), .Z(Z), .OutSignal(microcontroller_1_outsignal), .Drivers(Dr_spl_in),
    .Loaders(Ld_spl_in), .Writers({WrMEM, WrREG}), .ALU(func), .RegSel(regno), .Clock(CLK));
  assign bit_extender_1_out = {{11{microcontroller_1_outsignal[4]}}, microcontroller_1_outsignal};  // Bit_Extender bit_extender_1

  // Notes on the sheet:
  //   Loaders
  //   Drivers
endmodule

module ALUx16 (
  input  [15:0] A,
  input  [15:0] B,
  input  [1:0] func,
  output [15:0] \output 
);

  wire [15:0] adder_1_out, adder_2_out, demultiplexer_1_out0, demultiplexer_1_out1, demultiplexer_1_out2,
       demultiplexer_1_out3, demultiplexer_2_out0, demultiplexer_2_out1, demultiplexer_2_out2,
       demultiplexer_2_out3, nand_1_out, subtractor_1_out;

  Adder #(.width(16)) adder_1 (
    .a(demultiplexer_1_out0), .b(demultiplexer_2_out0), .out(adder_1_out));  // open: cin, cout
  Demultiplexer #(.select(2), .width(16), .enable("false")) demultiplexer_1 (
    .out0(demultiplexer_1_out0), .out1(demultiplexer_1_out1), .out2(demultiplexer_1_out2),
    .out3(demultiplexer_1_out3), .in(A), .sel(func));
  assign nand_1_out = ~(demultiplexer_1_out1 & demultiplexer_2_out1);  // NAND_Gate nand_1, 16 bits wide
  Subtractor #(.width(16)) subtractor_1 (
    .a(demultiplexer_1_out2), .b(demultiplexer_2_out2), .out(subtractor_1_out));  // open: bin, bout
  Multiplexer #(.select(2), .width(16), .enable("false")) multiplexer_1 (
    .in0(adder_1_out), .in1(nand_1_out), .in2(subtractor_1_out), .in3(adder_2_out), .out(\output ), .sel(func));
  Demultiplexer #(.select(2), .width(16), .enable("false")) demultiplexer_2 (
    .out0(demultiplexer_2_out0), .out1(demultiplexer_2_out1), .out2(demultiplexer_2_out2),
    .out3(demultiplexer_2_out3), .in(B), .sel(func));
  Adder #(.width(16)) adder_2 (.a(demultiplexer_1_out3), .b(16'h1), .out(adder_2_out));  // open: cin, cout
  // also tied to GND on the sheet: {demultiplexer_2_out3[0], demultiplexer_2_out3[1], demultiplexer_2_out3[2], demultiplexer_2_out3[3], demultiplexer_2_out3[4], demultiplexer_2_out3[5], demultiplexer_2_out3[6], demultiplexer_2_out3[7], demultiplexer_2_out3[8], demultiplexer_2_out3[9], demultiplexer_2_out3[10], demultiplexer_2_out3[11], demultiplexer_2_out3[12], demultiplexer_2_out3[13], demultiplexer_2_out3[14], demultiplexer_2_out3[15]}
endmodule

module register_array (
  input  CLK,
  input  WrREG,
  input  [3:0] regno,
  input  [15:0] Din,
  output [15:0] Dout
);

  wire reg0_en, reg1_en, reg2_en, reg3_en, reg4_en, reg5_en, reg6_en, reg7_en, reg8_en, reg9_en, reg10_en,
       reg11_en, reg12_en, reg13_en, reg14_en, reg15_en, smalland_1_out_3, smalland_2_out_3,
       smalland_3_out_3, smalland_4_out_3, smalland_5_out_3, smalland_6_out_3, smalland_7_out_3,
       smalland_8_out_3, smalland_9_out_3, smalland_10_out_3, smalland_11_out_3, smalland_12_out_3,
       smalland_13_out_3, smalland_14_out_3, smalland_15_out_3, smalland_16_out_3;
  wire [15:0] out0, out1, out2, out3, out4, out5, out6, out7, out8, out9, out10, out11, out12, out13, out14,
       out15;

  Decoder #(.select(4), .enable("false")) decoder_1 (
    .out0(reg0_en), .out1(reg1_en), .out2(reg2_en), .out3(reg3_en), .out4(reg4_en), .out5(reg5_en),
    .out6(reg6_en), .out7(reg7_en), .out8(reg8_en), .out9(reg9_en), .out10(reg10_en), .out11(reg11_en),
    .out12(reg12_en), .out13(reg13_en), .out14(reg14_en), .out15(reg15_en), .sel(regno));
  smallAnd smalland_1 (.in_1(reg0_en), .in_2(WrREG), .out_3(smalland_1_out_3));
  smallAnd smalland_2 (.in_1(reg4_en), .in_2(WrREG), .out_3(smalland_2_out_3));
  smallAnd smalland_3 (.in_1(reg8_en), .in_2(WrREG), .out_3(smalland_3_out_3));
  smallAnd smalland_4 (.in_1(reg12_en), .in_2(WrREG), .out_3(smalland_4_out_3));
  Multiplexer #(.select(4), .width(16), .enable("false")) multiplexer_1 (
    .in0(out0), .in1(out1), .in2(out2), .in3(out3), .in4(out4), .in5(out5), .in6(out6), .in7(out7),
    .in8(out8), .in9(out9), .in10(out10), .in11(out11), .in12(out12), .in13(out13), .in14(out14),
    .in15(out15), .out(Dout), .sel(regno));
  Register #(.width(16)) zero (.D(Din), .en(smalland_1_out_3), .Q(out0), .clk(CLK), .clr(1'b1));
  Register #(.width(16)) a1 (.D(Din), .en(smalland_2_out_3), .Q(out4), .clk(CLK));  // open: clr
  Register #(.width(16)) t2 (.D(Din), .en(smalland_3_out_3), .Q(out8), .clk(CLK));  // open: clr
  Register #(.width(16)) k0 (.D(Din), .en(smalland_4_out_3), .Q(out12), .clk(CLK));  // open: clr
  smallAnd smalland_5 (.in_1(reg1_en), .in_2(WrREG), .out_3(smalland_5_out_3));
  smallAnd smalland_6 (.in_1(reg5_en), .in_2(WrREG), .out_3(smalland_6_out_3));
  smallAnd smalland_7 (.in_1(reg9_en), .in_2(WrREG), .out_3(smalland_7_out_3));
  smallAnd smalland_8 (.in_1(reg13_en), .in_2(WrREG), .out_3(smalland_8_out_3));
  Register #(.width(16)) at (.D(Din), .en(smalland_5_out_3), .Q(out1), .clk(CLK));  // open: clr
  Register #(.width(16)) a2 (.D(Din), .en(smalland_6_out_3), .Q(out5), .clk(CLK));  // open: clr
  Register #(.width(16)) s0 (.D(Din), .en(smalland_7_out_3), .Q(out9), .clk(CLK));  // open: clr
  Register #(.width(16)) sp (.D(Din), .en(smalland_8_out_3), .Q(out13), .clk(CLK));  // open: clr
  Register #(.width(16)) v0 (.D(Din), .en(smalland_9_out_3), .Q(out2), .clk(CLK));  // open: clr
  smallAnd smalland_9 (.in_1(reg2_en), .in_2(WrREG), .out_3(smalland_9_out_3));
  Register #(.width(16)) t0 (.D(Din), .en(smalland_10_out_3), .Q(out6), .clk(CLK));  // open: clr
  smallAnd smalland_10 (.in_1(reg6_en), .in_2(WrREG), .out_3(smalland_10_out_3));
  Register #(.width(16)) s1 (.D(Din), .en(smalland_11_out_3), .Q(out10), .clk(CLK));  // open: clr
  smallAnd smalland_11 (.in_1(reg10_en), .in_2(WrREG), .out_3(smalland_11_out_3));
  Register #(.width(16)) fp (.D(Din), .en(smalland_12_out_3), .Q(out14), .clk(CLK));  // open: clr
  smallAnd smalland_12 (.in_1(reg14_en), .in_2(WrREG), .out_3(smalland_12_out_3));
  smallAnd smalland_13 (.in_1(reg3_en), .in_2(WrREG), .out_3(smalland_13_out_3));
  smallAnd smalland_14 (.in_1(reg7_en), .in_2(WrREG), .out_3(smalland_14_out_3));
  smallAnd smalland_15 (.in_1(reg11_en), .in_2(WrREG), .out_3(smalland_15_out_3));
  smallAnd smalland_16 (.in_1(reg15_en), .in_2(WrREG), .out_3(smalland_16_out_3));
  Register #(.width(16)) a0 (.D(Din), .en(smalland_13_out_3), .Q(out3), .clk(CLK));  // open: clr
  Register #(.width(16)) t1 (.D(Din), .en(smalland_14_out_3), .Q(out7), .clk(CLK));  // open: clr
  Register #(.width(16)) s2 (.D(Din), .en(smalland_15_out_3), .Q(out11), .clk(CLK));  // open: clr
  Register #(.width(16)) ra (.D(Din), .en(smalland_16_out_3), .Q(out15), .clk(CLK));  // open: clr
endmodule

module microcontroller (
  input  [15:0] Input_x16,
  input  Z,
  input  Clock,
  output [4:0] OutSignal,
  output [4:0] Drivers,
  output [3:0] RegSel,
  output [5:0] Loaders,
  output [1:0] Writers,
  output [1:0] ALU
);

  wire [5:0] multiplexer_1_out, rom_1_data, rom_2_data, rom_3_data, StateREG_q;
  wire [24:19] rom_1_data_2;

  ROM #(.addrWidth(6), .dataWidth(25)) rom_1 (
    .addr(StateREG_q),
    .data({rom_1_data_2[24:23], ALU, rom_1_data_2[20:19], Writers, Loaders, Drivers, rom_1_data}));  // open: sel
  Multiplexer #(.select(2), .width(6), .enable("false")) multiplexer_1 (
    .in0(rom_1_data), .in1(rom_2_data), .in2(rom_3_data), .in3({6{1'b0}}), .out(multiplexer_1_out),
    .sel(rom_1_data_2[24:23]));
  Register #(.width(6)) StateREG (.D(multiplexer_1_out), .Q(StateREG_q), .clk(Clock));  // open: en, clr
  Multiplexer #(.select(2), .width(4), .enable("false")) multiplexer_2 (
    .in0(Input_x16[12:9]), .in1(Input_x16[8:5]),
    .in2({Input_x16[0], Input_x16[1], Input_x16[2], Input_x16[3]}), .out(RegSel), .sel(rom_1_data_2[20:19]));  // open: in3
  ROM #(.addrWidth(3), .dataWidth(6)) rom_2 (.addr(Input_x16[15:13]), .data(rom_2_data));  // open: sel
  ROM #(.addrWidth(2), .dataWidth(6)) rom_3 (.addr({1'b0, Z}), .data(rom_3_data));  // open: sel

  assign OutSignal = Input_x16[4:0];

  // Notes on the sheet:
  //   Main ROM
  //   NextState[0-5]
  //   Drivers[R,M,A,P,O]
  //   Loaders[P,I,M,A,B,Z]
  //   Writers[R,M]
  //   RegSelLo/Hi
  //   ALULo/Hi
  //   OpTest+ChkZ
  //   contents of rom_1 (hex, n*v repeats v):
  //   6201 1082 e00900 84044 108045 20100 84047 108048 220100 8404a 840b 20100 8404d 840e 210f 20080 84051
  //   8412 2113 40040 4055 88056 1410100 4218 8419 900 0 a021c 840 1d 1e
  //   OpCheck ROM (seq ROM)
  //   contents of rom_2 (hex, n*v repeats v):
  //   3 6 9 c 10 14 1b 1d
  //   Opcode
  //   RX
  //   RY
  //   RZ
  //   OnZ ROM (beq ROM)
  //   Offset
  //   contents of rom_3 (hex, n*v repeats v):
  //   1a 17
endmodule

module Dr_split (
  input  [4:0] Input,
  output DrOFF,
  output DrPC,
  output DrALU,
  output DrMEM,
  output DrREG
);


  assign DrALU = Input[2];
  assign DrMEM = Input[1];
  assign DrOFF = Input[4];
  assign DrPC = Input[3];
  assign DrREG = Input[0];
endmodule

module Ld_split (
  input  [5:0] Input,
  output LdPC,
  output LdIR,
  output LdMAR,
  output LdA,
  output LdB,
  output LdZ
);


  assign LdA = Input[3];
  assign LdB = Input[4];
  assign LdIR = Input[1];
  assign LdMAR = Input[2];
  assign LdPC = Input[0];
  assign LdZ = Input[5];
endmodule

module smallAnd (
  input  in_1,
  input  in_2,
  output out_3
);

  and and_1 (out_3, in_1, in_2);
endmodule
